# Fritzing sketch arduino_ll_sketch (saved by Fritzing 0.8.7b)
breadboards: 1

parts:
  Part1 = Arduino Uno (Rev3)
  LED1 = LED - 5mm [color="Yellow (592nm)" package="5 mm [THT]"]
  R1 = Resistor [tolerance=±5% resistance=220 package=THT]
  S1 = Pushbutton [package="[THT]"]
  R2 = Resistor [tolerance=±5% resistance=220 package=THT]
  J1 = Basic Servo

nets:
  N1: Part1.D8, LED1.anode
  N2: Part1.D9_PWM, J1.pulse
  N3: Part1.D2, S1.Pin_3, S1.Pin_4, R2.Pin_1
  5V: Part1.5V, S1.Pin_1, S1.Pin_2, J1.vcc
  GND: Part1.GND, R1.Pin_0, R2.Pin_0, J1.gnd
  N4: LED1.cathode, R1.Pin_1
